# Fritzing sketch схема (saved by Fritzing 0.9.5d)
circuit board: 8.46667cm x 5.64444cm
breadboards: 1

parts:
  S1 = Pushbutton [package="[THT]"]
  S2 = Pushbutton [package="[THT]"]
  S3 = Pushbutton [package="[THT]"]
  S4 = Pushbutton [package="[THT]"]
  S5 = Pushbutton [package="[THT]"]
  S6 = Pushbutton [package="[THT]"]
  Компонент1 = Arduino Micro (Rev3)  # not connected
  Компонент2 = ws2812b [package="smd 2812b"]
  Компонент3 = ws2812b [package="smd 2812b"]
  Компонент4 = ws2812b [package="smd 2812b"]
  Компонент5 = ws2812b [package="smd 2812b"]
  Компонент6 = ws2812b [package="smd 2812b"]
  Компонент7 = ws2812b [package="smd 2812b"]

nets:
  VDD: S1.Pin_1, S1.Pin_2, S2.Pin_1, S2.Pin_2, S3.Pin_1, S3.Pin_2, S4.Pin_1, S4.Pin_2, S5.Pin_1, S5.Pin_2, S6.Pin_1, S6.Pin_2, Компонент2.VDD, Компонент3.VDD, Компонент4.VDD, Компонент5.VDD, Компонент6.VDD, Компонент7.VDD
  N1: S1.Pin_3, S1.Pin_4
  N2: S2.Pin_3, S2.Pin_4
  N3: S3.Pin_3, S3.Pin_4
  N4: S4.Pin_3, S4.Pin_4
  N5: S5.Pin_3, S5.Pin_4
  N6: S6.Pin_3, S6.Pin_4
  N7: Компонент2.DOUT, Компонент3.DIN
  VSS: Компонент2.VSS, Компонент3.VSS, Компонент4.VSS, Компонент5.VSS, Компонент6.VSS, Компонент7.VSS
  N8: Компонент2.DIN, Компонент7.DOUT
  N9: Компонент4.DOUT, Компонент6.DIN
  N10: Компонент5.DOUT, Компонент7.DIN
  N11: Компонент5.DIN, Компонент6.DOUT
